# Fritzing sketch relojv01 (saved by Fritzing 0.9.1b)
breadboards: 2
stripboards: 1

parts:
  LED1 = RGB LED (com. cathode, rgb) [package="5 mm [THT]"]  # not connected
  Parte1 = Arduino Uno (Rev3)  # not connected
  Q1 = NPN-Transistor [package="TO92 [THT]"]  # not connected
  Q2 = NPN-Transistor [package="TO92 [THT]"]  # not connected
  Q3 = NPN-Transistor [package="TO92 [THT]"]  # not connected
  J1 = male pin header, 24 pins [form="♂ (male)"]
  J2 = male pin header, 24 pins [form="♂ (male)"]
  J3 = male pin header, 24 pins [form="♂ (male)"]
  J4 = male pin header, 24 pins [form="♂ (male)"]
  TLC5940NT3 = TLC5940NT [package="DIP (Dual Inline)"]
  TLC5940NT4 = TLC5940NT [package="DIP (Dual Inline)"]
  Parte4 = Arduino Mega Proto Shield
  R1 = Resistor [tolerance=±5% resistance=47 package="1206 [SMD]"]  # not connected
  R2 = Resistor [tolerance=±5% resistance=47 package="1206 [SMD]"]  # not connected
  J5 = female pin header, 10 pins [form="♀ (female)"]  # not connected
  J6 = female pin header, 6 pins [form="♀ (female)"]  # not connected
  J7 = female pin header, 10 pins [form="♀ (female)"]  # not connected
  U1 = MOSFET-PCHANNEL-SOIC8 [package=so08]  # not connected
  Q4 = Basic FET P-Channel [package="TO220 [THT]"]
  Q5 = Basic FET P-Channel [package="TO220 [THT]"]
  Q6 = Basic FET P-Channel [package="TO220 [THT]"]
  Q7 = MOSFET-NCHANNEL [package=to-92]  # not connected
  LED4 = RGB LED (com. anode, rbg) [package="5 mm [THT]"]  # not connected
  R3 = Resistor [tolerance=±5% resistance=47 package="1206 [SMD]"]  # not connected
  J10 = male pin header, 4 pins [form="♂ (male)"]
  J11 = male pin header, 4 pins [form="♂ (male)"]
  J12 = male pin header, 4 pins [form="♂ (male)"]
  J13 = male pin header, 4 pins [form="♂ (male)"]
  J14 = male pin header, 4 pins [form="♂ (male)"]
  J15 = male pin header, 4 pins [form="♂ (male)"]
  J16 = male pin header, 4 pins [form="♂ (male)"]
  J17 = male pin header, 4 pins [form="♂ (male)"]
  J18 = male pin header, 4 pins [form="♂ (male)"]
  J19 = male pin header, 4 pins [form="♂ (male)"]
  J20 = male pin header, 4 pins [form="♂ (male)"]
  J21 = male pin header, 4 pins [form="♂ (male)"]
  J22 = male pin header, 4 pins [form="♂ (male)"]
  J23 = male pin header, 4 pins [form="♂ (male)"]
  J24 = male pin header, 4 pins [form="♂ (male)"]
  J25 = male pin header, 4 pins [form="♂ (male)"]
  J26 = male pin header, 4 pins [form="♂ (male)"]
  J27 = male pin header, 4 pins [form="♂ (male)"]
  J28 = male pin header, 4 pins [form="♂ (male)"]
  J29 = male pin header, 4 pins [form="♂ (male)"]
  J30 = male pin header, 4 pins [form="♂ (male)"]
  J31 = male pin header, 4 pins [form="♂ (male)"]
  J32 = male pin header, 4 pins [form="♂ (male)"]
  J33 = male pin header, 4 pins [form="♂ (male)"]
  R4 = Resistor [tolerance=±5% resistance=680 package=THT]
  R5 = Resistor [tolerance=±5% resistance=680 package=THT]
  R6 = TRIMPOT [package=3362u-2]
  R7 = TRIMPOT [package=3362u-2]
  R8 = TRIMPOT [package=3362u-2]

nets:
  N1: J1.pin1, J2.pin1, J3.pin1, J4.pin1
  N2: J1.pin2, J2.pin2, J3.pin2, J4.pin2
  N3: J1.pin3, J2.pin3, J3.pin3, J4.pin3
  N4: J1.pin4, J2.pin4, J3.pin4, J4.pin4
  N5: J1.pin5, J1.pin6, J1.pin7, J2.pin5, J2.pin6, J2.pin7, J3.pin5, J3.pin6, J3.pin7, J4.pin5, J4.pin6, J4.pin7
  N6: J1.pin8, J2.pin8, J3.pin8, J4.pin8
  N7: J1.pin9, J2.pin9, J3.pin9, J4.pin9
  N8: J1.pin10, J1.pin11, J1.pin12, J1.pin13, J1.pin14, J2.pin10, J2.pin11, J2.pin12, J2.pin13, J2.pin14, J3.pin10, J3.pin11, J3.pin12, J3.pin13, J3.pin14, J4.pin10, J4.pin11, J4.pin12, J4.pin13, J4.pin14
  N9: J1.pin15, J1.pin16, J2.pin15, J2.pin16, J3.pin15, J3.pin16, J4.pin15, J4.pin16
  N10: J1.pin17, J2.pin17, J3.pin17, J4.pin17
  N11: J1.pin18, J2.pin18, J3.pin18, J4.pin18
  N12: J1.pin19, J2.pin19, J3.pin19, J4.pin19
  N13: J1.pin20, J2.pin20, J3.pin20, J4.pin20
  N14: J1.pin21, J2.pin21, J3.pin21, J4.pin21
  N15: J1.pin22, J2.pin22, J3.pin22, J4.pin22
  N16: J1.pin23, J2.pin23, J3.pin23, J4.pin23
  N17: J1.pin24, J2.pin24, J3.pin24, J4.pin24
  N18: TLC5940NT3.OUT1, Parte4.N$183
  N19: TLC5940NT3.OUT2, Parte4.N$172
  N20: TLC5940NT3.OUT3, Parte4.N$155
  N21: TLC5940NT3.OUT4, Parte4.N$144
  N22: TLC5940NT3.OUT5, Parte4.N$129
  N23: TLC5940NT3.OUT6, Parte4.N$115
  N24: TLC5940NT3.OUT7, Parte4.N$102
  N25: TLC5940NT3.OUT8, Parte4.N$91
  N26: TLC5940NT3.OUT9, Parte4.N$78
  N27: TLC5940NT3.OUT10, Parte4.N$67
  N28: TLC5940NT3.OUT11, Parte4.N$54
  N29: TLC5940NT3.OUT12, Parte4.N$43
  N30: TLC5940NT3.OUT13, Parte4.N$30
  N31: TLC5940NT3.OUT14, Parte4.N$19
  N32: TLC5940NT3.OUT15, Parte4.N$16
  N33: TLC5940NT3.XERR, Parte4.N$33
  N34: TLC5940NT3.SOUT, Parte4.N$40
  N35: TLC5940NT3.GSCLK, TLC5940NT4.GSCLK, Parte4.D3, Parte4.N$57, Parte4.N$270
  VCC: TLC5940NT3.DCPRG, TLC5940NT3.VCC, TLC5940NT4.DCPRG, TLC5940NT4.VCC, Parte4.5V, Parte4.N$64, Parte4.N$88, Parte4.N$281, Parte4.N$309
  N36: TLC5940NT3.IREF, Parte4.N$81, Parte4.N$83, R4.Pin_0
  GND: TLC5940NT3.GND, TLC5940NT3.VPRG, TLC5940NT4.GND, TLC5940NT4.VPRG, Parte4.GND, Parte4.N$35, Parte4.N$105, Parte4.N$169, Parte4.N$243, Parte4.N$331, Parte4.N$413, R4.Pin_1, R5.Pin_1
  N37: TLC5940NT3.BLANK, TLC5940NT4.BLANK, Parte4.D10, Parte4.N$112, Parte4.N$350
  N38: TLC5940NT3.XLAT, TLC5940NT4.XLAT, Parte4.D9, Parte4.N$132, Parte4.N$364
  N39: TLC5940NT3.SCLK, TLC5940NT4.SCLK, Parte4.D13, Parte4.N$141, Parte4.N$383
  N40: TLC5940NT3.SIN, TLC5940NT4.SOUT, Parte4.N$158, Parte4.N$253
  N41: TLC5940NT3.OUT0, Parte4.N$186
  N42: TLC5940NT4.OUT1, Parte4.N$446
  N43: TLC5940NT4.OUT2, Parte4.N$440
  N44: TLC5940NT4.OUT3, Parte4.N$427
  N45: TLC5940NT4.OUT4, Parte4.N$380
  N46: TLC5940NT4.OUT5, Parte4.N$366
  N47: TLC5940NT4.OUT6, Parte4.N$347
  N48: TLC5940NT4.OUT7, Parte4.N$334
  N49: TLC5940NT4.OUT8, Parte4.N$325
  N50: TLC5940NT4.OUT9, Parte4.N$295
  N51: TLC5940NT4.OUT10, Parte4.N$283
  N52: TLC5940NT4.OUT11, Parte4.N$267
  N53: TLC5940NT4.OUT12, Parte4.N$256
  N54: TLC5940NT4.OUT13, Parte4.N$239
  N55: TLC5940NT4.OUT14, Parte4.N$228
  N56: TLC5940NT4.OUT15, Parte4.N$225
  N57: TLC5940NT4.XERR, Parte4.N$242
  N58: TLC5940NT4.IREF, Parte4.N$298, Parte4.N$299, R5.Pin_0
  N59: TLC5940NT4.SIN, Parte4.D11, Parte4.N$424
  N60: TLC5940NT4.OUT0, Parte4.N$412
  N61: Parte4.5V@1, Parte4.N$464, Parte4.N$466, Parte4.N$467, J21.pin1, J21.pin3, J21.pin4
  N62: Parte4.N$1, J13.pin4
  N63: Parte4.N$8, Q4.gate
  N64: Parte4.N$9, Q4.drain
  N65: Parte4.N$10, Q4.source
  N66: Parte4.N$12, J12.pin4
  N67: Parte4.N$20, Q6.gate
  N68: Parte4.N$21, Q6.drain
  N69: Parte4.N$22, Q6.source
  N70: Parte4.N$27, Q5.source
  N71: Parte4.N$28, Q5.drain
  N72: Parte4.N$29, Q5.gate
  N73: Parte4.N$44, R8.CW
  N74: Parte4.N$46, R7.CW
  N75: Parte4.N$47, R6.CW
  N76: Parte4.N$50, R6.WIPER
  N77: Parte4.N$51, R7.WIPER
  N78: Parte4.N$53, R8.WIPER
  N79: Parte4.N$68, Parte4.N$101, J32.pin1, R8.CCW
  N80: Parte4.N$70, Parte4.N$99, J32.pin3, R7.CCW
  N81: Parte4.N$71, Parte4.N$98, J32.pin4, R6.CCW
  N82: Parte4.N$100, J32.pin2
  N83: Parte4.N$116, J33.pin1
  N84: Parte4.N$117, J33.pin2
  N85: Parte4.N$118, J33.pin3
  N86: Parte4.N$119, J33.pin4
  N87: Parte4.N$122, J22.pin4
  N88: Parte4.N$123, J22.pin3
  N89: Parte4.N$124, J22.pin2
  N90: Parte4.N$128, J22.pin1
  N91: Parte4.N$145, J23.pin1
  N92: Parte4.N$146, J23.pin2
  N93: Parte4.N$147, J23.pin3
  N94: Parte4.N$148, J23.pin4
  N95: Parte4.N$151, J24.pin4
  N96: Parte4.N$152, J24.pin3
  N97: Parte4.N$153, J24.pin2
  N98: Parte4.N$154, J24.pin1
  N99: Parte4.N$173, J25.pin1
  N100: Parte4.N$174, J25.pin2
  N101: Parte4.N$175, J25.pin3
  N102: Parte4.N$176, J25.pin4
  N103: Parte4.N$179, J26.pin4
  N104: Parte4.N$180, J26.pin3
  N105: Parte4.N$181, J26.pin2
  N106: Parte4.N$182, J26.pin1
  N107: Parte4.N$201, J27.pin1
  N108: Parte4.N$202, J27.pin2
  N109: Parte4.N$203, J27.pin3
  N110: Parte4.N$204, J27.pin4
  N111: Parte4.N$207, J28.pin4
  N112: Parte4.N$208, J28.pin3
  N113: Parte4.N$209, J28.pin2
  N114: Parte4.N$210, J28.pin1
  N115: Parte4.N$229, J30.pin1
  N116: Parte4.N$230, J30.pin2
  N117: Parte4.N$231, J30.pin3
  N118: Parte4.N$232, J30.pin4
  N119: Parte4.N$235, J29.pin4
  N120: Parte4.N$236, J29.pin3
  N121: Parte4.N$237, J29.pin2
  N122: Parte4.N$238, J29.pin1
  N123: Parte4.N$257, J31.pin1
  N124: Parte4.N$258, J31.pin2
  N125: Parte4.N$259, J31.pin3
  N126: Parte4.N$260, J31.pin4
  N127: Parte4.N$263, J11.pin4
  N128: Parte4.N$264, J11.pin3
  N129: Parte4.N$265, J11.pin2
  N130: Parte4.N$266, J11.pin1
  N131: Parte4.N$285, J10.pin1
  N132: Parte4.N$286, J10.pin2
  N133: Parte4.N$287, J10.pin3
  N134: Parte4.N$288, J10.pin4
  N135: Parte4.N$292, J12.pin3
  N136: Parte4.N$293, J12.pin2
  N137: Parte4.N$294, J12.pin1
  N138: Parte4.N$312, J13.pin1
  N139: Parte4.N$313, J13.pin3
  N140: Parte4.N$324, J13.pin2
  N141: Parte4.N$335, J14.pin1
  N142: Parte4.N$336, J14.pin2
  N143: Parte4.N$337, J14.pin3
  N144: Parte4.N$338, J14.pin4
  N145: Parte4.N$343, J15.pin4
  N146: Parte4.N$344, J15.pin3
  N147: Parte4.N$345, J15.pin2
  N148: Parte4.N$346, J15.pin1
  N149: Parte4.N$368, J16.pin1
  N150: Parte4.N$369, J16.pin2
  N151: Parte4.N$370, J16.pin3
  N152: Parte4.N$371, J16.pin4
  N153: Parte4.N$376, J17.pin4
  N154: Parte4.N$377, J17.pin3
  N155: Parte4.N$378, J17.pin2
  N156: Parte4.N$379, J17.pin1
  N157: Parte4.N$428, J18.pin1
  N158: Parte4.N$429, J18.pin2
  N159: Parte4.N$430, J18.pin4
  N160: Parte4.N$431, J18.pin3
  N161: Parte4.N$436, J19.pin4
  N162: Parte4.N$437, J19.pin3
  N163: Parte4.N$438, J19.pin1
  N164: Parte4.N$439, J19.pin2
  N165: Parte4.N$460, J20.pin4
  N166: Parte4.N$461, J20.pin3
  N167: Parte4.N$462, J20.pin2
  N168: Parte4.N$463, J20.pin1
  N169: Parte4.N$465, J21.pin2

custom parts:
  TLC5940NT: The TLC5940 is a 16-channel, constant-current sink, LED driver. Each channel has an individually adjustable 4096-step grayscale PWM brightness control and a 64-step constant-current sink (dot correction).
